# Fritzing sketch kwikset (saved by Fritzing 0.9.3b)
breadboards: 1

parts:
  Raspberry_Pi_Zero1 = Raspberry Pi Zero
  M1 = DC Motor  # not connected
  S2 = Toggle Switch [package=THT]
  R1 = Resistor [tolerance=±5% resistance=220 package="2512 [SMD]"]
  R2 = Resistor [tolerance=±5% resistance=220 package="2512 [SMD]"]
  S3 = Toggle Switch [package=THT]
  Part2 = Arduino Pro Mini (5V)  # not connected

nets:
  N1: Raspberry_Pi_Zero1.GPIO19, R2.Pin_1, S3.L2
  N2: Raspberry_Pi_Zero1.GPIO26, S2.L2, R1.Pin_1
  N3: Raspberry_Pi_Zero1.GND, R1.Pin_0, R2.Pin_0

notes:
  Keypad
  - Orange - Input - Flash LED
  - Brown - Output - What key pressed
  - Red - +Voltage
  - Black - GND
  3V rail
  5V rail
  UART (serial) input
  Fully locked/unlocked sensors
